# Fritzing sketch Circuit (saved by Fritzing 0.9.3b)

parts:
  Display1 = LCD screen 16x2 IIC [part_number=101290]
  HC-SR04_Sensor_1 = HC-SR04 Ultrasonic Distance Sensor
  HC-SR04_Sensor_2 = HC-SR04 Ultrasonic Distance Sensor
  J1 = Power Jack [package=power_jack_smd]
  U2 = SWITCH-SPST-2 [package=r_sw_th]
  Part1 = Arduino Nano (Rev3.0) (ICSP)

nets:
  GND: Display1.GND, HC-SR04_Sensor_1.GND, HC-SR04_Sensor_2.GND, U2.O, Part1.GND
  VCC: Display1.VCC, HC-SR04_Sensor_1.VCC, HC-SR04_Sensor_2.VCC, Part1.5V
  N1: Display1.SDA, Part1.A4
  N2: Display1.SCL, Part1.A5
  N3: HC-SR04_Sensor_1.TRIG, Part1.D3
  N4: HC-SR04_Sensor_1.ECHO, Part1.D2
  N5: HC-SR04_Sensor_2.TRIG, Part1.D5
  N6: HC-SR04_Sensor_2.ECHO, Part1.D4
  GND_2: J1.GND, Part1.VIN
  N7: J1.GNDBREAK, U2.P

notes:
  Right
  Left

custom parts:
  LCD screen 16x2 IIC: LCD screen with HD44780 controller enables showing text, symbols, value or anything else that comes from Croduino/Arduino. It is capable of showing 16 symbols in two lines and therefore can be used in many projects that need to send clearly visible and legible output information.. • Color of symbols: White • Backlight: Blue • Dimensions: 80 x 36 x 12 mm • Screen dimensions: 64.5 x 16 mm •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
